# Fritzing sketch Piezoschematic (saved by Fritzing 0.4.3b)
breadboards: 1

parts:
  Netduino1 = Netduino
  R1 = Resistor [resistance=680 package=THT]
  J1 = Piezo Speaker

nets:
  N1: Netduino1.GND, J1.pin1
  N2: Netduino1.D5_PWM0, R1.Pin_0
  N3: R1.Pin_1, J1.pin2
